# Fritzing sketch ArduinoShield (saved by Fritzing 0.9.3b)
circuit board: 6.88566cm x 5.36311cm

parts:
  VCC1_->_L1 = Battery block 9V
  Q1 = MOSFET-NCHANNEL [package=to220v]
  Q2 = MOSFET-NCHANNEL [package=to220v]
  R1 = Resistor [tolerance=±5% resistance=100 package=THT]
  R2 = Resistor [tolerance=±5% resistance=10k package=THT]
  L1 = Solenoid
  R3 = Resistor [tolerance=±5% resistance=100 package=THT]
  R4 = Resistor [tolerance=±5% resistance=10k package=THT]
  L2 = Solenoid
  R5 = Resistor [tolerance=±5% resistance=10k package=THT]
  IC1 = SHIFT REGISTER [package=dil16]
  IC2 = SHIFT REGISTER [package=dil16]
  C1 = Ceramic Capacitor [capacitance=100nF package="100 mil [THT, multilayer]"]
  パーツ1 = Arduino Uno (Rev3)
  VCC2_->_L2 = DC Power [voltage=12V]
  SW1 = Toggle Switch [package=THT]
  R6 = Resistor [tolerance=±5% resistance=10k package=THT]
  SW2 = Basic Force Sensing Resistor (FSR) [package=THT]
  R7 = Resistor [tolerance=±5% resistance=10k package=THT]
  SW3 = Basic Force Sensing Resistor (FSR) [package=THT]
  R8 = Resistor [tolerance=±5% resistance=10k package=THT]

nets:
  GND: VCC1_->_L1.-, Q1.S, Q2.S, R2.Pin_1, R4.Pin_1, R5.Pin_1, IC1.GND, IC1.G, IC2.GND, IC2.G, C1.0, パーツ1.GND, VCC2_->_L2.V-, R6.Pin_1, R7.Pin_1, R8.Pin_1
  N1: VCC1_->_L1.+, L1.pin1
  N2: Q1.G, R1.Pin_1
  N3: Q1.D, L1.pin2
  N4: Q2.G, R3.Pin_1
  N5: Q2.D, L2.pin2
  N6: R1.Pin_0, R2.Pin_0, パーツ1.D3_PWM
  N7: R3.Pin_0, R4.Pin_0, パーツ1.D5_PWM
  N8: L2.pin1, VCC2_->_L2.V+
  N9: R5.Pin_0, パーツ1.D2, SW1.L1
  N10: IC1.QH*, IC2.SER
  VCC: IC1.SCL, IC1.VCC, IC2.SCL, IC2.VCC, パーツ1.5V, SW1.COM, SW2.pin_0, SW3.pin_0
  N11: IC1.SCK, IC2.SCK, パーツ1.D12/MISO
  N12: IC1.RCK, IC2.RCK, C1.1, パーツ1.D8
  N13: IC1.SER, パーツ1.D11_PWM/MOSI
  N14: パーツ1.D4, R6.Pin_0, SW2.pin_1
  N15: R7.Pin_0, SW3.pin_1

notes:
  off<->on
  No Connect
  PIN2:SW1
  PIN3:L1
  PIN5:L2
  5v->GND
  MOSFET->GND
  PIN08:Latch
  PIN11:Data
  PIN12:Clock
  SAME VCC
  VCC2 -> L2
  PIN2:SW
  PIN4:SW2
  +
  -
  SW4
  PIN
