# Fritzing sketch ArduinoShield_2 (saved by Fritzing 0.9.3b)
circuit board: 10cm x 10cm

parts:
  VCC1->L1 = Battery block 9V
  Q1 = MOSFET-NCHANNEL [package=to220v]
  Q2 = MOSFET-NCHANNEL [package=to220v]
  R1 = Resistor [tolerance=±5% resistance=100 package=THT]
  R2 = Resistor [tolerance=±5% resistance=10k package=THT]
  L1 = Solenoid
  R3 = Resistor [tolerance=±5% resistance=100 package=THT]
  R4 = Resistor [tolerance=±5% resistance=10k package=THT]
  L2 = Solenoid
  R5 = Resistor [tolerance=±5% resistance=10k package=THT]
  IC1 = SHIFT REGISTER [package=dil16]
  IC2 = SHIFT REGISTER [package=dil16]
  C1 = Ceramic Capacitor [capacitance=100nF package="100 mil [THT, multilayer]"]
  パーツ1 = Arduino Uno (Rev3)
  VCC2_->_L2 = DC Power [voltage=12V]
  SW1 = Toggle Switch [package=THT]
  R6 = Resistor [tolerance=±5% resistance=10k package=THT]
  SW2 = Basic Force Sensing Resistor (FSR) [package=THT]
  R7 = Resistor [tolerance=±5% resistance=10k package=THT]
  SW3 = Basic Force Sensing Resistor (FSR) [package=THT]
  R8 = Resistor [tolerance=±5% resistance=10k package=THT]
  D1 = Rectifier Diode [part_number=1N4001 package="300 mil [THT]"]
  D2 = Rectifier Diode [part_number=1N4001 package="300 mil [THT]"]
  パーツ2 = SO08 [chip_label=SO08 package=SO]
  パーツ3 = SO08 [chip_label=SO08 package=SO]
  パーツ4 = SO08 [chip_label=SO08 package=SO]
  パーツ5 = SO08 [chip_label=SO08 package=SO]
  SW(D8) = Basic Force Sensing Resistor (FSR) [package=THT]
  SW(A3) = Basic Force Sensing Resistor (FSR) [package=THT]
  10K = Resistor [tolerance=±5% resistance=10k package=THT]
  10K_2 = Resistor [tolerance=±5% resistance=10k package=THT]

nets:
  GND: VCC1->L1.-, Q1.S, Q2.S, R2.Pin_1, R4.Pin_1, R5.Pin_1, IC1.GND, IC1.G, IC2.GND, IC2.G, C1.0, パーツ1.GND, VCC2_->_L2.V-, R6.Pin_1, R7.Pin_1, R8.Pin_1
  N1: VCC1->L1.+, L1.pin1, D1.cathode
  N2: Q1.G, R1.Pin_1
  N3: Q1.D, L1.pin2, D1.anode
  N4: Q2.G, R3.Pin_1
  N5: Q2.D, L2.pin2, D2.anode
  N6: R1.Pin_0, R2.Pin_0, パーツ1.D3_PWM
  N7: R3.Pin_0, R4.Pin_0, パーツ1.D5_PWM
  N8: L2.pin1, VCC2_->_L2.V+, D2.cathode
  N9: R5.Pin_0, パーツ1.D2, SW1.L1
  N10: IC1.QH*, IC2.SER
  VCC: IC1.SCL, IC1.VCC, IC2.SCL, IC2.VCC, パーツ1.5V, SW1.COM, SW2.pin_0, SW3.pin_0
  N11: IC1.SCK, IC2.SCK, パーツ1.D12/MISO
  N12: IC1.RCK, IC2.RCK, C1.1, パーツ1.D8
  N13: IC1.SER, パーツ1.D11_PWM/MOSI
  N14: パーツ1.D4, R6.Pin_0, SW2.pin_1
  N15: R7.Pin_0, SW3.pin_1
  N16: パーツ2.1, パーツ2.3, パーツ3.1, パーツ3.3, パーツ4.1, パーツ4.3, パーツ5.1, パーツ5.3
  N17: パーツ2.5, パーツ2.6
  N18: パーツ2.7, パーツ2.8
  N19: パーツ3.5, パーツ3.6
  N20: パーツ3.7, パーツ3.8
  N21: パーツ4.5, パーツ4.6
  N22: パーツ4.7, パーツ4.8
  N23: パーツ5.5, パーツ5.6
  N24: パーツ5.7, パーツ5.8
  N25: SW(D8).pin_0, SW(A3).pin_0
  N26: SW(D8).pin_1, 10K_2.Pin_0
  N27: SW(A3).pin_1, 10K.Pin_0
  N28: 10K.Pin_1, 10K_2.Pin_1

notes:
  off<->on
  GND<-5V
  GND<-MOSFET
  SAME VCC
  VCC2->L2
  PIN2:SW
  +
  -
  SW4
  PIN
  GND
  5V
  3V3
  A0
  A1
  A2
  A3
  A4
  A5
  VIN
  RESET
  IOREF
  13
  Clock 12
  Data 11
  ~10
  ~09
  Latch08
  07
  ~06
  L2~05
  SW2 04
  L1~03
  SW1 02
  TX0->01
  RX0<-00
  G
  0
  7
  8
  15
  3
  4
  1
  5
  MPU6050
  Display
