# Fritzing sketch Shield_Nefry (saved by Fritzing 0.9.3b)
circuit board: 5cm x 4.5cm

parts:
  J1 = Basic Force Sensing Resistor (FSR) [package=THT]
  J2 = Basic Force Sensing Resistor (FSR) [package=THT]
  10K = Resistor [tolerance=±5% resistance=10k package=THT]
  10K_2 = Resistor [tolerance=±5% resistance=10k package=THT]
  10K_3 = Resistor [tolerance=±5% resistance=10k package=THT]
  10K_4 = Resistor [tolerance=±5% resistance=10k package=THT]
  J3 = Basic Force Sensing Resistor (FSR) [package=THT]
  J4 = Basic Force Sensing Resistor (FSR) [package=THT]

nets:
  N1: J1.pin_0, J2.pin_0, J3.pin_0, J4.pin_0
  N2: J1.pin_1, 10K_4.Pin_0
  N3: J2.pin_1, 10K.Pin_0
  N4: 10K.Pin_1, 10K_2.Pin_1, 10K_3.Pin_1, 10K_4.Pin_1
  N5: 10K_2.Pin_0, J4.pin_1
  N6: 10K_3.Pin_0, J3.pin_1

notes:
  PIN2:SW
  +
  PIN
  13
  07
  SW2 04
  0
  -
  3
  Display
  5V
  GND
  3.3V
  A3
  A2
  A1
  A0
  D8
  D7
  TX
  RX
  Reset
  D0
  D1
  D2
  D3
  D4
  D5
  D6
  Input(A3)
  Input(A2)
  Input(D8)
  Input(D7)
  NefryBT Shield
