# Fritzing sketch RotateLCD (saved by Fritzing 0.9.3b)
circuit board: 10cm x 6cm

parts:
  パーツ1 = Arduino Uno (Rev3)
  U1 = MCP41xxx [package=so08]
  JP1 = Header 4 [package=screwterminal-3.5mm-4_lock]
  JP2 = Header 4 [package=screwterminal-3.5mm-4_lock]
  J1 = JST-B3P-VH [part_number=JST-B3P-VH package=THT]
  VCC1->L1 = Battery block 9V

nets:
  N1: パーツ1.A0, JP1.3
  N2: パーツ1.A1, JP2.3
  N3: パーツ1.D10_PWM/SS, U1.CS
  N4: パーツ1.D11_PWM/MOSI, U1.DI
  N5: パーツ1.D13/SCK, U1.SCK
  GND: パーツ1.GND, U1.GND, JP1.2, JP2.2, VCC1->L1.-
  5V: パーツ1.5V, U1.VCC
  N6: U1.A, J1.pin3
  N7: U1.W, J1.pin2
  N8: U1.B, J1.pin1
  N9: JP1.1, JP2.1, VCC1->L1.+

notes:
  off<->on
  GND<-5V
  GND<-MOSFET
  SAME VCC
  VCC2->L2
  PIN2:SW
  +
  -
  SW4
  PIN
  GND
  5V
  3V3
  A0
  A1
  A2
  A3
  A4
  A5
  VIN
  RESET
  IOREF
  13
  Clock 12
  Data 11
  ~10
  ~09
  Latch08
  07
  ~06
  L2~05
  SW2 04
  L1~03
  SW1 02
  TX0->01
  RX0<-00
  G
  0
  7
  8
  15
  3
