# Fritzing sketch relayLED (saved by Fritzing 0.9.3b)
circuit board: 8cm x 8cm

parts:
  R1(100) = Resistor [tolerance=±5% resistance=100 package=THT]
  R3 = Resistor [tolerance=±5% resistance=100 package=THT]
  R5 = Resistor [tolerance=±5% resistance=100 package=THT]
  R2(15k) = Resistor [tolerance=±5% resistance=15k package=THT]
  R4 = Resistor [tolerance=±5% resistance=15k package=THT]
  R6 = Resistor [tolerance=±5% resistance=15k package=THT]
  LED1 = LED - 5mm [color="Red (633nm)" package="5 mm [THT]"]
  LED3 = LED - 5mm [color="Blue (525nm)" package="5 mm [THT]"]
  LED2 = LED - 5mm [color="Green (570nm)" package="5 mm [THT]"]
  JP1 = Header 2 [package=molex-1x2_lock]
  JP2 = Header 3 [package=molex-1x3_lock]
  JP3 = Header 3 [package=molex-1x3_lock]
  JP4 = Header 3 [package=molex-1x3_lock]
  JP5 = Header 1 [package=1x01_offset]
  Q1 = Basic FET N-Channel [package="TO220 [THT]"]
  Q3 = Basic FET N-Channel [package="TO220 [THT]"]
  Q2 = Basic FET N-Channel [package="TO220 [THT]"]
  Q5 = Basic FET N-Channel [package="TO220 [THT]"]
  Q6 = Basic FET N-Channel [package="TO220 [THT]"]
  Q4 = Basic FET N-Channel [package="TO220 [THT]"]
  R9 = Resistor [tolerance=±5% resistance=100 package=THT]
  R7 = Resistor [tolerance=±5% resistance=100 package=THT]
  R11 = Resistor [tolerance=±5% resistance=100 package=THT]
  R8 = Resistor [tolerance=±5% resistance=15k package=THT]
  R10 = Resistor [tolerance=±5% resistance=15k package=THT]
  R12 = Resistor [tolerance=±5% resistance=15k package=THT]
  LED6 = LED - 5mm [color="Blue (525nm)" package="5 mm [THT]"]
  LED4 = LED - 5mm [color="Red (633nm)" package="5 mm [THT]"]
  LED5 = LED - 5mm [color="Green (570nm)" package="5 mm [THT]"]
  Q8 = Basic FET N-Channel [package="TO220 [THT]"]
  Q9 = Basic FET N-Channel [package="TO220 [THT]"]
  Q7 = Basic FET N-Channel [package="TO220 [THT]"]
  R15 = Resistor [tolerance=±5% resistance=100 package=THT]
  R13 = Resistor [tolerance=±5% resistance=100 package=THT]
  R17 = Resistor [tolerance=±5% resistance=100 package=THT]
  R14 = Resistor [tolerance=±5% resistance=15k package=THT]
  R16 = Resistor [tolerance=±5% resistance=15k package=THT]
  R18 = Resistor [tolerance=±5% resistance=15k package=THT]
  LED9 = LED - 5mm [color="Blue (525nm)" package="5 mm [THT]"]
  LED7 = LED - 5mm [color="Red (633nm)" package="5 mm [THT]"]
  LED8 = LED - 5mm [color="Green (570nm)" package="5 mm [THT]"]

nets:
  N1: R1(100).Pin_0, JP2.1
  N2: R1(100).Pin_1, R2(15k).Pin_0, Q1.gate
  N3: R3.Pin_0, JP2.2
  N4: R3.Pin_1, R4.Pin_0, Q2.gate
  N5: R5.Pin_0, JP2.3
  N6: R5.Pin_1, R6.Pin_0, Q3.gate
  GND: R2(15k).Pin_1, R4.Pin_1, R6.Pin_1, JP1.2, JP5.1, Q1.source, Q3.source, Q2.source, Q5.source, Q6.source, Q4.source, R8.Pin_1, R10.Pin_1, R12.Pin_1, Q8.source, Q9.source, Q7.source, R14.Pin_1, R16.Pin_1, R18.Pin_1
  N7: LED1.cathode, Q1.drain
  N8: LED1.anode, LED3.anode, LED2.anode, JP1.1, LED6.anode, LED4.anode, LED5.anode, LED9.anode, LED7.anode, LED8.anode
  N9: LED3.cathode, Q3.drain
  N10: LED2.cathode, Q2.drain
  N11: JP3.1, R7.Pin_0
  N12: JP3.2, R9.Pin_0
  N13: JP3.3, R11.Pin_0
  N14: JP4.1, R13.Pin_0
  N15: JP4.2, R15.Pin_0
  N16: JP4.3, R17.Pin_0
  N17: Q5.gate, R9.Pin_1, R10.Pin_0
  N18: Q5.drain, LED5.cathode
  N19: Q6.gate, R11.Pin_1, R12.Pin_0
  N20: Q6.drain, LED6.cathode
  N21: Q4.gate, R7.Pin_1, R8.Pin_0
  N22: Q4.drain, LED4.cathode
  N23: Q8.gate, R15.Pin_1, R16.Pin_0
  N24: Q8.drain, LED8.cathode
  N25: Q9.gate, R17.Pin_1, R18.Pin_0
  N26: Q9.drain, LED9.cathode
  N27: Q7.gate, R13.Pin_1, R14.Pin_0
  N28: Q7.drain, LED7.cathode

notes:
  PIN2:SW
  +
  PIN
  13
  07
  SW2 04
  0
  -
  3
  Gate
  Drain
  Source
  Vcc
  GND
  1
  2
  5
  6
  4
  8
  7
  9
  INPUT SIGNAL
  Electronic Parts
  [No use]
