# Fritzing sketch N_MOSFET (saved by Fritzing 0.9.3b)
perfboards: 1

parts:
  パーツ1 = Arduino Uno (Rev3) - ICSP
  R1 = Resistor [tolerance=±5% resistance=100 package=THT]
  R2 = Resistor [tolerance=±5% resistance=15k package=THT]
  L1 = Solenoid
  D1 = Rectifier Diode [part_number=1N4001 package="300 mil [THT]"]
  L2 = Solenoid
  D2 = Rectifier Diode [part_number=1N4001 package="300 mil [THT]"]
  R3 = Resistor [tolerance=±5% resistance=100 package=THT]
  R4 = Resistor [tolerance=±5% resistance=15k package=THT]
  L3 = Solenoid
  D3 = Rectifier Diode [part_number=1N4001 package="300 mil [THT]"]
  R5 = Resistor [tolerance=±5% resistance=100 package=THT]
  R6 = Resistor [tolerance=±5% resistance=15k package=THT]
  L4 = Solenoid
  D4 = Rectifier Diode [part_number=1N4001 package="300 mil [THT]"]
  R7 = Resistor [tolerance=±5% resistance=100 package=THT]
  R8 = Resistor [tolerance=±5% resistance=15k package=THT]
  Power_plug1 = Power plug
  Q5 = Basic FET N-Channel [package="TO220 [THT]"]
  Q8 = Basic FET N-Channel [package="TO220 [THT]"]
  Q6 = Basic FET N-Channel [package="TO220 [THT]"]
  Q7 = Basic FET N-Channel [package="TO220 [THT]"]

nets:
  N1: パーツ1.D8, R1.Pin_1
  GND: パーツ1.GND, R2.Pin_0, R4.Pin_0, R6.Pin_0, R8.Pin_0, Power_plug1.GND, Q5.source, Q8.source, Q6.source, Q7.source
  N2: パーツ1.D5_PWM, R7.Pin_1
  N3: パーツ1.D6_PWM, R5.Pin_1
  N4: パーツ1.D7, R3.Pin_1
  N5: R1.Pin_0, R2.Pin_1, Q5.gate
  N6: L1.pin1, D1.anode, Q5.drain
  N7: L1.pin2, D1.cathode, L2.pin2, D2.cathode, L3.pin2, D3.cathode, L4.pin2, D4.cathode, Power_plug1.VCC
  N8: L2.pin1, D2.anode, Q6.drain
  N9: R3.Pin_0, R4.Pin_1, Q6.gate
  N10: L3.pin1, D3.anode, Q7.drain
  N11: R5.Pin_0, R6.Pin_1, Q7.gate
  N12: L4.pin1, D4.anode, Q8.drain
  N13: R7.Pin_0, R8.Pin_1, Q8.gate
